# Fritzing sketch pir_sparkfun_button (saved by Fritzing 1.0.5)
breadboards: 1

parts:
  Part7 = HC-SR501 Body Sensor Module
  R1 = Resistor [tolerance=±5% resistance=10k package="2010 [SMD]"]
  S2 = Pushbutton [package="[THT]"]
  R2 = Resistor [tolerance=±5% power=0.25 resistance=330 package=THT]
  A1 = Particle Photon 2

nets:
  N1: Part7.VCC, R1.Pin_1, A1.Pin_19
  N2: Part7.OUT, S2.Pin_1, S2.Pin_2
  N3: Part7.GND, R1.Pin_0, A1.Pin_26
  N4: S2.Pin_3, S2.Pin_4, R2.Pin_1, A1.Pin_25
  N5: A1.Pin_4, A1.Pin_30
  N6: A1.Pin_28, A1.Pin_29

notes:
  Note Sparkfun PIR wiring

custom parts:
  HC-SR501 Body Sensor Module: Pyroelectric Infrared PIR Motion Sensor Detector Module
  Particle Photon 2: The Photon 2 is a development module with a microcontroller and Wi-Fi networking. -- This Fritzing file originally created by Peter Van Epp https://forum.fritzing.org/t/request-particle-photon2/19824/2 5/18/2024 - Rob Parke Rotated breadboard image
